// Logisim project cpuddr.circ as structural Verilog: 7 circuits, main circuit top
module fulladd (
  input  in_1,
  input  in_2,
  input  in_3,
  output out_4,
  output out_5
);

  wire and_1_out, and_2_out, and_3_out;

  and and_1 (and_1_out, in_1, in_2);
  and and_2 (and_2_out, in_1, in_3);
  and and_3 (and_3_out, in_2, in_3);
  xor xor_1 (out_5, in_1, in_2, in_3);
  or or_1 (out_4, and_1_out, and_2_out, and_3_out);
endmodule

module add4 (
  input  [3:0] in_1,
  input  [3:0] in_2,
  input  in_3,
  output out_4,
  output [3:0] out_5
);

  wire fulladd_2_out_4, fulladd_3_out_4, fulladd_4_out_4;

  fulladd fulladd_1 (.in_1(in_1[3]), .in_2(in_2[3]), .in_3(fulladd_2_out_4), .out_4(out_4), .out_5(out_5[3]));
  fulladd fulladd_2 (.in_1(in_1[2]), .in_2(in_2[2]), .in_3(fulladd_3_out_4), .out_4(fulladd_2_out_4), .out_5(out_5[2]));
  fulladd fulladd_3 (.in_1(in_1[1]), .in_2(in_2[1]), .in_3(fulladd_4_out_4), .out_4(fulladd_3_out_4), .out_5(out_5[1]));
  fulladd fulladd_4 (.in_1(in_1[0]), .in_2(in_2[0]), .in_3(in_3), .out_4(fulladd_4_out_4), .out_5(out_5[0]));
endmodule

module leftshift8 (
  input  [7:0] in_1,
  output [7:0] out_2,
  output out_3
);


  assign out_2 = {in_1[6:0], 1'b0};
  assign out_3 = in_1[7];
endmodule

module alu8 (
  input  rsl,
  input  lsr,
  input  \xor ,
  input  \or ,
  input  \and ,
  input  add,
  input  sub,
  input  [7:0] b,
  input  [7:0] a,
  output [7:0] x,
  output cout,
  output zero,
  output sign
);

  wire adder_1_cout, leftshift8_1_out_3, or_2_out, rightshift8_1_out_2;
  wire [7:0] adder_1_out, and_1_out, bit_extender_1_out, leftshift8_1_out_2, or_1_out, rightshift8_1_out_3,
       xor_1_out, xor_2_out;

  assign bit_extender_1_out = {{7{sub}}, sub};  // Bit_Extender bit_extender_1
  assign xor_1_out = bit_extender_1_out ^ b;  // XOR_Gate xor_1, 8 bits wide
  Adder adder_1 (.a(xor_1_out), .b(a), .out(adder_1_out), .cin(sub), .cout(adder_1_cout));
  assign and_1_out = b & a;  // AND_Gate and_1, 8 bits wide
  assign or_1_out = b | a;  // OR_Gate or_1, 8 bits wide
  assign xor_2_out = b ^ a;  // XOR_Gate xor_2, 8 bits wide
  leftshift8 leftshift8_1 (.in_1(a), .out_2(leftshift8_1_out_2), .out_3(leftshift8_1_out_3));
  rightshift8 rightshift8_1 (.in_1(a), .out_3(rightshift8_1_out_3), .out_2(rightshift8_1_out_2));
  or or_2 (or_2_out, add, sub);
  assign cout = or_2_out ? adder_1_cout : 1'bz;  // Controlled_Buffer controlled_buffer_1
  assign cout = lsr ? leftshift8_1_out_3 : 1'bz;  // Controlled_Buffer controlled_buffer_2
  assign cout = rsl ? rightshift8_1_out_2 : 1'bz;  // Controlled_Buffer controlled_buffer_3
  assign {sign, x[6:0]} = or_2_out ? adder_1_out : 8'bz;  // Controlled_Buffer controlled_buffer_4
  assign {sign, x[6:0]} = \and  ? and_1_out : 8'bz;  // Controlled_Buffer controlled_buffer_5
  assign {sign, x[6:0]} = \or  ? or_1_out : 8'bz;  // Controlled_Buffer controlled_buffer_6
  assign {sign, x[6:0]} = \xor  ? xor_2_out : 8'bz;  // Controlled_Buffer controlled_buffer_7
  assign {sign, x[6:0]} = lsr ? leftshift8_1_out_2 : 8'bz;  // Controlled_Buffer controlled_buffer_8
  assign {sign, x[6:0]} = rsl ? rightshift8_1_out_3 : 8'bz;  // Controlled_Buffer controlled_buffer_9
  nor nor_1 (zero, x[0], x[1], x[2], x[3], x[5], x[6], sign, x[4]);

  assign x[7] = sign;
endmodule

module rightshift8 (
  input  [7:0] in_1,
  output out_2,
  output [7:0] out_3
);


  assign out_2 = in_1[0];
  assign out_3 = {1'b0, in_1[7:1]};
endmodule

module latch1 (
  input  in_1,
  input  in_2,
  input  in_3,
  output out_4
);

  wire and_1_out, and_2_out, nor_1_out, not_1_out, or_1_out;

  not not_1 (not_1_out, in_1);
  and and_1 (and_1_out, in_1, in_2);
  and and_2 (and_2_out, in_2, not_1_out);
  nor nor_1 (nor_1_out, and_1_out, out_4);
  nor nor_2 (out_4, nor_1_out, or_1_out);
  or or_1 (or_1_out, and_2_out, in_3);
endmodule

module top (
  output [15:0] out_1
);

  wire alu8_1_cout, alu8_1_sign, alu8_1_zero, and_1_out, and_2_out, and_3_out, and_4_out, and_5_out,
       and_6_out, and_7_out, and_8_out, and_9_out, and_10_out, and_11_out, and_12_out, and_13_out,
       and_14_out, and_15_out, and_16_out, and_17_out, and_18_out, and_19_out, and_20_out, and_21_out,
       and_22_out, and_23_out, and_24_out, and_25_out, and_26_out, buffer_1_out, button_1_out, clock_1_out,
       controlled_buffer_1_out, d_ff_1_qn, d_ff_2_q, d_ff_3_q, decoder_1_out0, decoder_1_out1,
       decoder_1_out2, decoder_1_out3, decoder_1_out4, decoder_1_out5, decoder_1_out6, or_1_out, or_2_out,
       xnor_1_out, xnor_2_out, xor_1_out, xor_2_out, xor_3_out;
  wire [1:0] register_3_q_2;
  wire [2:0] d_ff_4_q;
  wire [2:2] pull_resistor_1_node;
  wire [7:0] alu8_1_x, controlled_buffer_10_out, counter_1_q, multiplexer_1_out, multiplexer_2_out,
       multiplexer_3_out, register_1_q, register_2_q;
  wire [7:2] register_3_q;
  wire [11:11] not_4_out, not_5_out;
  wire [15:7] undriven;
  wire [15:11] not_1_out;
  wire [15:12] not_7_out;
  wire [15:15] not_3_out;

  Button button_1 (.out(button_1_out));
  Clock clock_1 (.out(clock_1_out));
  xor xor_1 (xor_1_out, clock_1_out, d_ff_1_qn);
  D_Flip_Flop #(.trigger("high")) d_ff_1 (
    .clk(button_1_out), .D(clock_1_out), .Qn(d_ff_1_qn));  // open: Q, preset, en, reset
  Multiplexer #(.select(2), .width(8), .enable("false")) multiplexer_1 (
    .in0(controlled_buffer_10_out), .in1(register_2_q), .in2(register_1_q), .out(multiplexer_1_out),
    .sel(out_1[15:14]));  // open: in3
  // Probe on multiplexer_1_out
  // Probe on multiplexer_2_out
  Multiplexer #(.select(2), .width(8), .enable("false")) multiplexer_2 (
    .in0(register_2_q), .in1(register_1_q), .in2({8{1'b0}}), .out(multiplexer_2_out), .sel(out_1[13:12]));  // open: in3
  Register register_1 (.D(alu8_1_x), .en(out_1[11]), .Q(register_1_q), .clk(xor_1_out), .clr(button_1_out));
  Register register_2 (.D(alu8_1_x), .en(out_1[10]), .Q(register_2_q), .clk(xor_1_out), .clr(button_1_out));
  D_Flip_Flop d_ff_2 (
    .clk(xor_1_out), .D(controlled_buffer_1_out), .Q(d_ff_2_q), .preset(button_1_out));  // open: Qn, en, reset
  and and_1 (and_1_out, d_ff_2_q, ~xor_1_out);  // AND_Gate
  and and_2 (and_2_out, and_1_out, and_9_out);
  assign controlled_buffer_1_out = and_5_out ? and_5_out : 1'bz;  // Controlled_Buffer controlled_buffer_1
  and and_3 (and_3_out, and_1_out, and_10_out);
  assign out_1 = and_4_out ? {undriven, 7'b0011011} : 16'bz;  // Controlled_Buffer controlled_buffer_2
  and and_4 (and_4_out, xor_1_out, d_ff_2_q);
  and and_5 (and_5_out, and_2_out, ~xnor_1_out);  // AND_Gate
  assign out_1 = and_5_out ? {not_1_out[15], register_3_q_2[0], 2'b10, not_1_out[11], register_3_q_2[1], 10'h8b} : 16'bz;  // Controlled_Buffer controlled_buffer_3
  assign controlled_buffer_1_out = and_3_out ? and_3_out : 1'bz;  // Controlled_Buffer controlled_buffer_4
  assign out_1 = and_3_out ? {4'b0010, not_4_out[11], register_3_q_2[1], 7'b0010000, register_3_q_2[0], 2'b11} : 16'bz;  // Controlled_Buffer controlled_buffer_5
  and and_6 (and_6_out, and_1_out, and_11_out);
  assign controlled_buffer_1_out = and_6_out ? and_6_out : 1'bz;  // Controlled_Buffer controlled_buffer_6
  assign out_1 = and_6_out ? {not_3_out[15], register_3_q_2[0], 11'h418, register_3_q_2[1], 2'b10} : 16'bz;  // Controlled_Buffer controlled_buffer_7
  Decoder #(.select(3), .enable("false")) decoder_1 (
    .out0(decoder_1_out0), .out1(decoder_1_out1), .out2(decoder_1_out2), .out3(decoder_1_out3),
    .out4(decoder_1_out4), .out5(decoder_1_out5), .out6(decoder_1_out6), .sel(out_1[9:7]));  // open: out7
  xnor xnor_1 (xnor_1_out, register_3_q_2[1], register_3_q_2[0]);
  not not_1 (not_1_out[11], register_3_q_2[1]);
  not not_2 (not_1_out[15], register_3_q_2[0]);
  not not_3 (not_3_out[15], register_3_q_2[0]);
  alu8 alu8_1 (
    .rsl(decoder_1_out6), .lsr(decoder_1_out5), .\xor (decoder_1_out4), .\or (decoder_1_out3),
    .\and (decoder_1_out2), .add(decoder_1_out1), .sub(decoder_1_out0), .b(multiplexer_1_out),
    .a(multiplexer_2_out), .x(alu8_1_x), .cout(alu8_1_cout), .zero(alu8_1_zero), .sign(alu8_1_sign));
  and and_7 (and_7_out, xnor_1_out, and_2_out);
  assign controlled_buffer_1_out = and_7_out ? and_7_out : 1'bz;  // Controlled_Buffer controlled_buffer_8
  assign out_1 = and_7_out ? {4'b0010, not_5_out[11], register_3_q_2[1], 10'h9b} : 16'bz;  // Controlled_Buffer controlled_buffer_9
  not not_4 (not_4_out[11], register_3_q_2[1]);
  not not_5 (not_5_out[11], register_3_q_2[1]);
  // Probe on alu8_1_x
  Counter counter_1 (
    .load(out_1[5]), .D(alu8_1_x), .count(out_1[4]), .Q(counter_1_q), .clk(xor_2_out), .clr(button_1_out));  // open: carry
  xor xor_2 (xor_2_out, buffer_1_out, xor_1_out);
  D_Flip_Flop d_ff_3 (.clk(xor_1_out), .D(and_8_out), .Q(d_ff_3_q), .reset(button_1_out));  // open: Qn, preset, en
  and and_8 (and_8_out, d_ff_2_q, ~controlled_buffer_1_out);  // AND_Gate
  assign controlled_buffer_10_out = out_1[6] ? alu8_1_x : 8'bz;  // Controlled_Buffer controlled_buffer_10
  buf buffer_1 (buffer_1_out, xor_1_out);
  // Probe on multiplexer_3_out
  Multiplexer #(.select(2), .width(8), .enable("false")) multiplexer_3 (
    .in0(register_1_q), .in1(register_2_q), .in2(counter_1_q), .out(multiplexer_3_out), .sel(out_1[3:2]));  // open: in3
  D_Flip_Flop d_ff_4 (
    .clk(xor_1_out), .D(alu8_1_zero), .Q(d_ff_4_q[0]), .en(pull_resistor_1_node[2]), .reset(button_1_out));  // open: Qn, preset
  D_Flip_Flop d_ff_5 (
    .clk(xor_1_out), .D(alu8_1_cout), .Q(d_ff_4_q[1]), .en(pull_resistor_1_node[2]), .reset(button_1_out));  // open: Qn, preset
  D_Flip_Flop d_ff_6 (
    .clk(xor_1_out), .D(alu8_1_sign), .Q(d_ff_4_q[2]), .en(pull_resistor_1_node[2]), .reset(button_1_out));  // open: Qn, preset
  Pull_Resistor pull_resistor_1 (.node(pull_resistor_1_node[2]));
  RAM ram_1 (
    .addr(multiplexer_3_out), .data(controlled_buffer_10_out), .sel(out_1[1]), .clk(xor_1_out), .ld(out_1[0]));  // open: clr
  // Probe on controlled_buffer_10_out
  Register #(.trigger("falling")) register_3 (
    .D(controlled_buffer_10_out), .en(d_ff_2_q), .Q({register_3_q, register_3_q_2}), .clk(xor_1_out),
    .clr(button_1_out));
  // Probe on {register_3_q, register_3_q_2}
  and and_9 (and_9_out, ~register_3_q[2], ~register_3_q[3], ~register_3_q[4], ~register_3_q[5], ~register_3_q[6], ~register_3_q[7]);  // AND_Gate
  and and_10 (and_10_out, register_3_q[2], ~register_3_q[3], ~register_3_q[4], ~register_3_q[5], ~register_3_q[6], ~register_3_q[7]);  // AND_Gate
  and and_11 (and_11_out, ~register_3_q[2], register_3_q[3], ~register_3_q[4], ~register_3_q[5], ~register_3_q[6], ~register_3_q[7]);  // AND_Gate
  and and_12 (and_12_out, and_1_out, and_25_out);
  assign controlled_buffer_1_out = and_12_out ? 1'b1 : 1'bz;  // Controlled_Buffer controlled_buffer_11
  assign out_1 = or_1_out ? 16'h20ab : 16'bz;  // Controlled_Buffer controlled_buffer_12
  and and_13 (and_13_out, and_1_out, and_26_out);
  and and_14 (and_14_out, and_13_out, ~xnor_2_out);  // AND_Gate
  assign controlled_buffer_1_out = and_14_out ? and_14_out : 1'bz;  // Controlled_Buffer controlled_buffer_13
  and and_15 (and_15_out, and_12_out, register_3_q[2], register_3_q_2[1], ~register_3_q_2[0]);  // AND_Gate
  or or_1 (or_1_out, and_15_out, xor_3_out);
  assign {3{pull_resistor_1_node[2]}} = and_14_out ? 3'b111 : 3'bz;  // Controlled_Buffer controlled_buffer_14
  assign out_1 = and_14_out ? {not_7_out[15], register_3_q_2[0], 1'b0, {2{not_7_out[12]}}, register_3_q_2[1], 2'b00, register_3_q[3], 7'b0001011} : 16'bz;  // Controlled_Buffer controlled_buffer_15
  and and_16 (and_16_out, and_12_out, ~register_3_q[2], ~register_3_q_2[1]);  // AND_Gate
  and and_17 (and_17_out, and_12_out, ~register_3_q[2], register_3_q_2[1]);  // AND_Gate
  and and_18 (and_18_out, and_16_out, d_ff_4_q[0]);
  or or_2 (or_2_out, and_18_out, and_21_out, and_20_out);
  xor xor_3 (xor_3_out, or_2_out, and_22_out);
  not not_6 (not_7_out[12], register_3_q_2[1]);
  not not_7 (not_7_out[15], register_3_q_2[0]);
  and and_19 (and_19_out, and_12_out, register_3_q[2], ~register_3_q_2[1]);  // AND_Gate
  and and_20 (and_20_out, and_19_out, d_ff_4_q[1]);
  and and_21 (and_21_out, and_17_out, ~d_ff_4_q[0], ~d_ff_4_q[1]);  // AND_Gate
  xnor xnor_2 (xnor_2_out, register_3_q_2[1], register_3_q_2[0]);
  and and_22 (and_22_out, and_12_out, register_3_q_2[0]);
  and and_23 (and_23_out, and_12_out, ~or_1_out);  // AND_Gate
  assign out_1 = and_23_out ? 16'h1b : 16'bz;  // Controlled_Buffer controlled_buffer_16
  and and_24 (and_24_out, xnor_2_out, and_13_out);
  assign controlled_buffer_1_out = and_24_out ? and_24_out : 1'bz;  // Controlled_Buffer controlled_buffer_17
  assign {3{pull_resistor_1_node[2]}} = and_24_out ? 3'b111 : 3'bz;  // Controlled_Buffer controlled_buffer_18
  assign out_1 = and_24_out ? {3'b000, {2{not_7_out[12]}}, register_3_q_2[1], 2'b00, register_3_q[3], 7'b0011011} : 16'bz;  // Controlled_Buffer controlled_buffer_19
  and and_25 (and_25_out, ~register_3_q[3], ~register_3_q[4], register_3_q[5], ~register_3_q[6], ~register_3_q[7]);  // AND_Gate
  and and_26 (and_26_out, register_3_q[4], ~register_3_q[5], ~register_3_q[6], ~register_3_q[7]);  // AND_Gate

  // Notes on the sheet:
  //   rega
  //   regb
  //   mov [r],r
  //   mov r,imm / r,r
  //   ip
  //   mov r,[r]
  //   _inlat
  //   jz
  //   ja
  //   add/sub r,r/r,imm
  //   jumps
  //   jb
endmodule
