// Logisim project cputest1.circ as structural Verilog: 7 circuits, main circuit top
module fulladd (
  input  in_1,
  input  in_2,
  input  in_3,
  output out_4,
  output out_5
);

  wire and_1_out, and_2_out, and_3_out;

  and and_1 (and_1_out, in_1, in_2);
  and and_2 (and_2_out, in_1, in_3);
  and and_3 (and_3_out, in_2, in_3);
  xor xor_1 (out_5, in_1, in_2, in_3);
  or or_1 (out_4, and_1_out, and_2_out, and_3_out);
endmodule

module add4 (
  input  [3:0] in_1,
  input  [3:0] in_2,
  input  in_3,
  output out_4,
  output [3:0] out_5
);

  wire fulladd_2_out_4, fulladd_3_out_4, fulladd_4_out_4;

  fulladd fulladd_1 (.in_1(in_1[3]), .in_2(in_2[3]), .in_3(fulladd_2_out_4), .out_4(out_4), .out_5(out_5[3]));
  fulladd fulladd_2 (.in_1(in_1[2]), .in_2(in_2[2]), .in_3(fulladd_3_out_4), .out_4(fulladd_2_out_4), .out_5(out_5[2]));
  fulladd fulladd_3 (.in_1(in_1[1]), .in_2(in_2[1]), .in_3(fulladd_4_out_4), .out_4(fulladd_3_out_4), .out_5(out_5[1]));
  fulladd fulladd_4 (.in_1(in_1[0]), .in_2(in_2[0]), .in_3(in_3), .out_4(fulladd_4_out_4), .out_5(out_5[0]));
endmodule

module alu8 (
  input  rsl,
  input  lsr,
  input  \xor ,
  input  \or ,
  input  \and ,
  input  addsub,
  input  sub,
  input  [7:0] b,
  input  [7:0] a,
  output [7:0] x,
  output cout
);

  wire [7:0] adder_1_out, and_1_out, bit_extender_1_out, leftshift8_1_out_2, or_1_out, rightshift8_1_out_2,
       xor_1_out, xor_2_out;

  assign bit_extender_1_out = {{7{sub}}, sub};  // Bit_Extender bit_extender_1
  assign xor_1_out = bit_extender_1_out ^ b;  // XOR_Gate xor_1, 8 bits wide
  Adder adder_1 (.a(xor_1_out), .b(a), .out(adder_1_out), .cin(sub), .cout(cout));
  assign and_1_out = b & a;  // AND_Gate and_1, 8 bits wide
  assign or_1_out = b | a;  // OR_Gate or_1, 8 bits wide
  assign xor_2_out = b ^ a;  // XOR_Gate xor_2, 8 bits wide
  leftshift8 leftshift8_1 (.in_1(a), .out_2(leftshift8_1_out_2));
  rightshift8 rightshift8_1 (.in_1(a), .out_2(rightshift8_1_out_2));
  assign x = addsub ? adder_1_out : 8'bz;  // Controlled_Buffer controlled_buffer_1
  assign x = \and  ? and_1_out : 8'bz;  // Controlled_Buffer controlled_buffer_2
  assign x = \or  ? or_1_out : 8'bz;  // Controlled_Buffer controlled_buffer_3
  assign x = \xor  ? xor_2_out : 8'bz;  // Controlled_Buffer controlled_buffer_4
  assign x = lsr ? leftshift8_1_out_2 : 8'bz;  // Controlled_Buffer controlled_buffer_5
  assign x = rsl ? rightshift8_1_out_2 : 8'bz;  // Controlled_Buffer controlled_buffer_6
endmodule

module leftshift8 (
  input  [7:0] in_1,
  output [7:0] out_2
);


  assign out_2 = {in_1[6:0], 1'b0};
endmodule

module rightshift8 (
  input  [7:0] in_1,
  output [7:0] out_2
);


  assign out_2 = {1'b0, in_1[7:1]};
endmodule

module top (
  input  in_1,
  input  in_2
);

  wire and_1_out, d_ff_1_q, or_1_out, or_2_out, or_3_out, or_4_out, or_5_out, or_6_out, or_7_out, or_8_out,
       or_9_out, or_10_out, or_11_out, or_12_out, or_13_out, or_14_out, or_15_out, or_16_out, or_17_out,
       or_18_out, or_19_out, or_20_out, or_21_out, or_22_out, or_23_out, undriven, undriven_2;
  wire [7:0] alu8_1_x, controlled_buffer_1_out, controlled_buffer_2_out, controlled_buffer_7_out,
       controlled_buffer_8_out, counter_1_q, register_1_q, register_2_q;
  wire [7:4] undriven_3;

  buf or_1 (or_1_out, 1'b0);  // OR_Gate
  buf or_2 (or_2_out, 1'b0);  // OR_Gate
  // Probe on controlled_buffer_2_out
  // Probe on controlled_buffer_1_out
  assign controlled_buffer_1_out = or_1_out ? {8{1'b0}} : 8'bz;  // Controlled_Buffer controlled_buffer_1
  Register register_1 (.D(alu8_1_x), .en(or_2_out), .Q(register_1_q), .clk(in_2), .clr(in_1));
  Register register_2 (.D(alu8_1_x), .en(or_3_out), .Q(register_2_q), .clk(in_2), .clr(in_1));
  buf or_3 (or_3_out, 1'b0);  // OR_Gate
  assign controlled_buffer_2_out = or_4_out ? register_1_q : 8'bz;  // Controlled_Buffer controlled_buffer_2
  assign controlled_buffer_1_out = or_5_out ? register_1_q : 8'bz;  // Controlled_Buffer controlled_buffer_3
  assign controlled_buffer_2_out = or_6_out ? register_2_q : 8'bz;  // Controlled_Buffer controlled_buffer_4
  D_Flip_Flop d_ff_1 (.clk(undriven_2), .Q(d_ff_1_q), .preset(undriven), .en(1'b1));  // open: D, Qn, reset
  D_Flip_Flop d_ff_2 (.clk(undriven_2), .D(and_1_out), .en(1'b1), .reset(undriven));  // open: Q, Qn, preset
  assign controlled_buffer_1_out = or_7_out ? register_2_q : 8'bz;  // Controlled_Buffer controlled_buffer_5
  buf or_4 (or_4_out, 1'b0);  // OR_Gate
  D_Flip_Flop d_ff_3 ();  // open: clk, D, Q, Qn, preset, en, reset
  alu8 alu8_1 (
    .rsl(or_14_out), .lsr(or_13_out), .\xor (or_12_out), .\or (or_11_out), .\and (or_10_out),
    .addsub(or_9_out), .sub(or_8_out), .b(controlled_buffer_2_out), .a(controlled_buffer_1_out), .x(alu8_1_x));  // open: cout
  buf or_5 (or_5_out, 1'b0);  // OR_Gate
  assign controlled_buffer_2_out = or_17_out ? controlled_buffer_7_out : 8'bz;  // Controlled_Buffer controlled_buffer_6
  // Probe on alu8_1_x
  Counter counter_1 (
    .load(or_15_out), .D(alu8_1_x), .count(or_16_out), .Q(counter_1_q), .clk(in_2), .clr(in_1));  // open: carry
  buf or_6 (or_6_out, 1'b0);  // OR_Gate
  assign controlled_buffer_7_out = or_18_out ? alu8_1_x : 8'bz;  // Controlled_Buffer controlled_buffer_7
  assign controlled_buffer_8_out = or_21_out ? register_1_q : 8'bz;  // Controlled_Buffer controlled_buffer_8
  buf or_7 (or_7_out, 1'b0);  // OR_Gate
  and and_1 (and_1_out, undriven_3[4], undriven_3[5], d_ff_1_q, undriven_3[6], undriven_3[7]);
  assign controlled_buffer_8_out = or_22_out ? register_2_q : 8'bz;  // Controlled_Buffer controlled_buffer_9
  assign controlled_buffer_8_out = or_23_out ? counter_1_q : 8'bz;  // Controlled_Buffer controlled_buffer_10
  buf or_8 (or_8_out, 1'b0);  // OR_Gate
  RAM ram_1 (
    .addr(controlled_buffer_8_out), .data(controlled_buffer_7_out), .sel(or_19_out), .clk(in_2),
    .ld(or_20_out));  // open: clr
  buf or_9 (or_9_out, 1'b0);  // OR_Gate
  buf or_10 (or_10_out, 1'b0);  // OR_Gate
  buf or_11 (or_11_out, 1'b0);  // OR_Gate
  buf or_12 (or_12_out, 1'b0);  // OR_Gate
  buf or_13 (or_13_out, 1'b0);  // OR_Gate
  buf or_14 (or_14_out, 1'b0);  // OR_Gate
  buf or_15 (or_15_out, 1'b0);  // OR_Gate
  buf or_16 (or_16_out, 1'b0);  // OR_Gate
  buf or_17 (or_17_out, 1'b0);  // OR_Gate
  buf or_18 (or_18_out, 1'b0);  // OR_Gate
  buf or_19 (or_19_out, 1'b0);  // OR_Gate
  buf or_20 (or_20_out, 1'b0);  // OR_Gate
  buf or_21 (or_21_out, 1'b0);  // OR_Gate
  buf or_22 (or_22_out, 1'b0);  // OR_Gate
  buf or_23 (or_23_out, 1'b0);  // OR_Gate
endmodule

module latch1 (
  input  in_1,
  input  in_2,
  input  in_3,
  output out_4
);

  wire and_1_out, and_2_out, nor_1_out, not_1_out, or_1_out;

  not not_1 (not_1_out, in_1);
  and and_1 (and_1_out, in_1, in_2);
  and and_2 (and_2_out, in_2, not_1_out);
  nor nor_1 (nor_1_out, and_1_out, out_4);
  nor nor_2 (out_4, nor_1_out, or_1_out);
  or or_1 (or_1_out, and_2_out, in_3);
endmodule
