// Logisim project cputest4.circ as structural Verilog: 7 circuits, main circuit top
module fulladd (
  input  in_1,
  input  in_2,
  input  in_3,
  output out_4,
  output out_5
);

  wire and_1_out, and_2_out, and_3_out;

  and and_1 (and_1_out, in_1, in_2);
  and and_2 (and_2_out, in_1, in_3);
  and and_3 (and_3_out, in_2, in_3);
  xor xor_1 (out_5, in_1, in_2, in_3);
  or or_1 (out_4, and_1_out, and_2_out, and_3_out);
endmodule

module add4 (
  input  [3:0] in_1,
  input  [3:0] in_2,
  input  in_3,
  output out_4,
  output [3:0] out_5
);

  wire fulladd_2_out_4, fulladd_3_out_4, fulladd_4_out_4;

  fulladd fulladd_1 (.in_1(in_1[3]), .in_2(in_2[3]), .in_3(fulladd_2_out_4), .out_4(out_4), .out_5(out_5[3]));
  fulladd fulladd_2 (.in_1(in_1[2]), .in_2(in_2[2]), .in_3(fulladd_3_out_4), .out_4(fulladd_2_out_4), .out_5(out_5[2]));
  fulladd fulladd_3 (.in_1(in_1[1]), .in_2(in_2[1]), .in_3(fulladd_4_out_4), .out_4(fulladd_3_out_4), .out_5(out_5[1]));
  fulladd fulladd_4 (.in_1(in_1[0]), .in_2(in_2[0]), .in_3(in_3), .out_4(fulladd_4_out_4), .out_5(out_5[0]));
endmodule

module leftshift8 (
  input  [7:0] in_1,
  output [7:0] out_2
);


  assign out_2 = {in_1[6:0], 1'b0};
endmodule

module alu8 (
  input  rsl,
  input  lsr,
  input  \xor ,
  input  \or ,
  input  \and ,
  input  add,
  input  sub,
  input  [7:0] b,
  input  [7:0] a,
  output [7:0] x,
  output cout
);

  wire or_2_out;
  wire [7:0] adder_1_out, and_1_out, bit_extender_1_out, leftshift8_1_out_2, or_1_out, rightshift8_1_out_2,
       xor_1_out, xor_2_out;

  assign bit_extender_1_out = {{7{sub}}, sub};  // Bit_Extender bit_extender_1
  assign xor_1_out = bit_extender_1_out ^ b;  // XOR_Gate xor_1, 8 bits wide
  Adder adder_1 (.a(xor_1_out), .b(a), .out(adder_1_out), .cin(sub), .cout(cout));
  assign and_1_out = b & a;  // AND_Gate and_1, 8 bits wide
  assign or_1_out = b | a;  // OR_Gate or_1, 8 bits wide
  assign xor_2_out = b ^ a;  // XOR_Gate xor_2, 8 bits wide
  leftshift8 leftshift8_1 (.in_1(a), .out_2(leftshift8_1_out_2));
  rightshift8 rightshift8_1 (.in_1(a), .out_2(rightshift8_1_out_2));
  or or_2 (or_2_out, add, sub);
  assign x = or_2_out ? adder_1_out : 8'bz;  // Controlled_Buffer controlled_buffer_1
  assign x = \and  ? and_1_out : 8'bz;  // Controlled_Buffer controlled_buffer_2
  assign x = \or  ? or_1_out : 8'bz;  // Controlled_Buffer controlled_buffer_3
  assign x = \xor  ? xor_2_out : 8'bz;  // Controlled_Buffer controlled_buffer_4
  assign x = lsr ? leftshift8_1_out_2 : 8'bz;  // Controlled_Buffer controlled_buffer_5
  assign x = rsl ? rightshift8_1_out_2 : 8'bz;  // Controlled_Buffer controlled_buffer_6
endmodule

module rightshift8 (
  input  [7:0] in_1,
  output [7:0] out_2
);


  assign out_2 = {1'b0, in_1[7:1]};
endmodule

module latch1 (
  input  in_1,
  input  in_2,
  input  in_3,
  output out_4
);

  wire and_1_out, and_2_out, nor_1_out, not_1_out, or_1_out;

  not not_1 (not_1_out, in_1);
  and and_1 (and_1_out, in_1, in_2);
  and and_2 (and_2_out, in_2, not_1_out);
  nor nor_1 (nor_1_out, and_1_out, out_4);
  nor nor_2 (out_4, nor_1_out, or_1_out);
  or or_1 (or_1_out, and_2_out, in_3);
endmodule

module top (
  output [15:0] out_1
);

  wire and_1_out, and_2_out, and_3_out, and_4_out, and_5_out, and_6_out, and_7_out, and_8_out, button_1_out,
       clock_1_out, controlled_buffer_2_out, d_ff_1_q, d_ff_2_q, d_ff_3_q, decoder_1_out0, decoder_1_out1,
       decoder_1_out2, decoder_1_out3, decoder_1_out4, decoder_1_out5, decoder_1_out6, xnor_1_out;
  wire [1:0] register_3_q_2;
  wire [7:0] alu8_1_x, controlled_buffer_6_out, counter_1_q, multiplexer_1_out, multiplexer_2_out,
       multiplexer_3_out, register_1_q, register_2_q;
  wire [7:2] register_3_q;
  wire [15:11] not_1_out;

  Button button_1 (.out(button_1_out));
  Clock clock_1 (.out(clock_1_out));
  Multiplexer #(.select(2), .width(8), .enable("false")) multiplexer_1 (
    .in0(controlled_buffer_6_out), .in1(register_2_q), .in2(register_1_q), .out(multiplexer_1_out),
    .sel(out_1[15:14]));  // open: in3
  // Probe on multiplexer_1_out
  // Probe on multiplexer_2_out
  Multiplexer #(.select(2), .width(8), .enable("false")) multiplexer_2 (
    .in0(register_2_q), .in1(register_1_q), .in2({8{1'b0}}), .out(multiplexer_2_out), .sel(out_1[13:12]));  // open: in3
  and and_1 (and_1_out, d_ff_2_q, ~controlled_buffer_2_out);  // AND_Gate
  Register register_1 (.D(alu8_1_x), .en(out_1[11]), .Q(register_1_q), .clk(clock_1_out), .clr(button_1_out));
  Register register_2 (.D(alu8_1_x), .en(out_1[10]), .Q(register_2_q), .clk(clock_1_out), .clr(button_1_out));
  assign out_1 = d_ff_2_q ? 16'h1b : 16'bz;  // Controlled_Buffer controlled_buffer_1
  D_Flip_Flop d_ff_1 (.clk(clock_1_out), .D(and_1_out), .Q(d_ff_1_q), .reset(button_1_out));  // open: Qn, preset, en
  and and_2 (and_2_out, d_ff_1_q, and_6_out);
  assign controlled_buffer_2_out = and_3_out ? and_3_out : 1'bz;  // Controlled_Buffer controlled_buffer_2
  and and_3 (and_3_out, and_2_out, ~xnor_1_out);  // AND_Gate
  not not_1 (not_1_out[11], register_3_q_2[1]);
  assign out_1 = and_3_out ? {not_1_out[15], register_3_q_2[0], 2'b10, not_1_out[11], register_3_q_2[1], 10'h81} : 16'bz;  // Controlled_Buffer controlled_buffer_3
  Decoder #(.select(3), .enable("false")) decoder_1 (
    .out0(decoder_1_out0), .out1(decoder_1_out1), .out2(decoder_1_out2), .out3(decoder_1_out3),
    .out4(decoder_1_out4), .out5(decoder_1_out5), .out6(decoder_1_out6), .sel(out_1[9:7]));  // open: out7
  xnor xnor_1 (xnor_1_out, register_3_q_2[1], register_3_q_2[0]);
  not not_2 (not_1_out[15], register_3_q_2[0]);
  alu8 alu8_1 (
    .rsl(decoder_1_out6), .lsr(decoder_1_out5), .\xor (decoder_1_out4), .\or (decoder_1_out3),
    .\and (decoder_1_out2), .add(decoder_1_out1), .sub(decoder_1_out0), .b(multiplexer_1_out),
    .a(multiplexer_2_out), .x(alu8_1_x));  // open: cout
  and and_4 (and_4_out, xnor_1_out, and_2_out);
  assign controlled_buffer_2_out = and_4_out ? and_4_out : 1'bz;  // Controlled_Buffer controlled_buffer_4
  assign out_1 = and_4_out ? {4'b0010, not_1_out[15], register_3_q_2[0], 10'h9b} : 16'bz;  // Controlled_Buffer controlled_buffer_5
  D_Flip_Flop d_ff_2 (
    .clk(clock_1_out), .D(controlled_buffer_2_out), .Q(d_ff_2_q), .preset(button_1_out));  // open: Qn, en, reset
  assign controlled_buffer_2_out = d_ff_2_q ? ~d_ff_2_q : 1'bz;  // Controlled_Inverter controlled_inverter_1
  // Probe on alu8_1_x
  Counter counter_1 (
    .load(out_1[5]), .D(alu8_1_x), .count(out_1[4]), .Q(counter_1_q), .clk(clock_1_out), .clr(button_1_out));  // open: carry
  D_Flip_Flop d_ff_3 (.clk(clock_1_out), .D(and_5_out), .Q(d_ff_3_q), .reset(button_1_out));  // open: Qn, preset, en
  and and_5 (and_5_out, d_ff_1_q, ~controlled_buffer_2_out);  // AND_Gate
  assign controlled_buffer_6_out = out_1[6] ? alu8_1_x : 8'bz;  // Controlled_Buffer controlled_buffer_6
  // Probe on multiplexer_3_out
  Multiplexer #(.select(2), .width(8), .enable("false")) multiplexer_3 (
    .in0(register_1_q), .in1(register_2_q), .in2(counter_1_q), .out(multiplexer_3_out), .sel(out_1[3:2]));  // open: in3
  Register register_3 (
    .D(controlled_buffer_6_out), .en(d_ff_2_q), .Q({register_3_q, register_3_q_2}), .clk(clock_1_out));  // open: clr
  RAM ram_1 (
    .addr(multiplexer_3_out), .data(controlled_buffer_6_out), .sel(out_1[1]), .clk(clock_1_out), .ld(out_1[0]));  // open: clr
  // Probe on controlled_buffer_6_out
  // Probe on {register_3_q, register_3_q_2}
  and and_6 (and_6_out, ~register_3_q[2], ~register_3_q[3], ~register_3_q[4], ~register_3_q[5], ~register_3_q[6], ~register_3_q[7]);  // AND_Gate
  and and_7 (and_7_out, register_3_q[2], ~register_3_q[3], ~register_3_q[4], ~register_3_q[5], ~register_3_q[6], ~register_3_q[7]);  // AND_Gate
  and and_8 (and_8_out, ~register_3_q[2], register_3_q[3], ~register_3_q[4], ~register_3_q[5], ~register_3_q[6], ~register_3_q[7]);  // AND_Gate

  // Notes on the sheet:
  //   rega
  //   regb
  //   ip
  //   _inlat
endmodule
