// Logisim project stream2.circ as structural Verilog: 7 circuits, main circuit top
module fulladd (
  input  in_1,
  input  in_2,
  input  in_3,
  output out_4,
  output out_5
);

  wire and_1_out, and_2_out, and_3_out;

  and and_1 (and_1_out, in_1, in_2);
  and and_2 (and_2_out, in_1, in_3);
  and and_3 (and_3_out, in_2, in_3);
  xor xor_1 (out_5, in_1, in_2, in_3);
  or or_1 (out_4, and_1_out, and_2_out, and_3_out);
endmodule

module add4 (
  input  [3:0] in_1,
  input  [3:0] in_2,
  input  in_3,
  output out_4,
  output [3:0] out_5
);

  wire fulladd_2_out_4, fulladd_3_out_4, fulladd_4_out_4;

  fulladd fulladd_1 (.in_1(in_1[3]), .in_2(in_2[3]), .in_3(fulladd_2_out_4), .out_4(out_4), .out_5(out_5[3]));
  fulladd fulladd_2 (.in_1(in_1[2]), .in_2(in_2[2]), .in_3(fulladd_3_out_4), .out_4(fulladd_2_out_4), .out_5(out_5[2]));
  fulladd fulladd_3 (.in_1(in_1[1]), .in_2(in_2[1]), .in_3(fulladd_4_out_4), .out_4(fulladd_3_out_4), .out_5(out_5[1]));
  fulladd fulladd_4 (.in_1(in_1[0]), .in_2(in_2[0]), .in_3(in_3), .out_4(fulladd_4_out_4), .out_5(out_5[0]));
endmodule

module alu8 (
  input  rsl,
  input  lsr,
  input  \xor ,
  input  \or ,
  input  \and ,
  input  addsub,
  input  sub,
  input  [7:0] b,
  input  [7:0] a,
  output [7:0] x,
  output cout
);

  wire [7:0] adder_1_out, and_1_out, bit_extender_1_out, leftshift8_1_out_2, or_1_out, rightshift8_1_out_2,
       xor_1_out, xor_2_out;

  assign bit_extender_1_out = {{7{sub}}, sub};  // Bit_Extender bit_extender_1
  assign xor_1_out = bit_extender_1_out ^ b;  // XOR_Gate xor_1, 8 bits wide
  Adder adder_1 (.a(xor_1_out), .b(a), .out(adder_1_out), .cin(sub), .cout(cout));
  assign and_1_out = b & a;  // AND_Gate and_1, 8 bits wide
  assign or_1_out = b | a;  // OR_Gate or_1, 8 bits wide
  assign xor_2_out = b ^ a;  // XOR_Gate xor_2, 8 bits wide
  leftshift8 leftshift8_1 (.in_1(a), .out_2(leftshift8_1_out_2));
  rightshift8 rightshift8_1 (.in_1(a), .out_2(rightshift8_1_out_2));
  assign x = addsub ? adder_1_out : 8'bz;  // Controlled_Buffer controlled_buffer_1
  assign x = \and  ? and_1_out : 8'bz;  // Controlled_Buffer controlled_buffer_2
  assign x = \or  ? or_1_out : 8'bz;  // Controlled_Buffer controlled_buffer_3
  assign x = \xor  ? xor_2_out : 8'bz;  // Controlled_Buffer controlled_buffer_4
  assign x = lsr ? leftshift8_1_out_2 : 8'bz;  // Controlled_Buffer controlled_buffer_5
  assign x = rsl ? rightshift8_1_out_2 : 8'bz;  // Controlled_Buffer controlled_buffer_6
endmodule

module leftshift8 (
  input  [7:0] in_1,
  output [7:0] out_2
);


  assign out_2 = {in_1[6:0], 1'b0};
endmodule

module rightshift8 (
  input  [7:0] in_1,
  output [7:0] out_2
);


  assign out_2 = {1'b0, in_1[7:1]};
endmodule

module top (
  input  [7:0] in_1,
  input  in_2,
  input  in_3,
  input  in_4,
  input  in_5,
  input  in_6,
  input  in_7,
  input  in_8,
  input  in_9,
  input  in_10,
  input  in_11,
  input  in_12,
  input  in_13,
  input  in_14,
  input  in_15,
  input  in_16,
  input  in_17,
  input  in_18,
  output [7:0] out_19
);

  wire [7:0] controlled_buffer_1_out, controlled_buffer_2_out, register_1_q, register_2_q;

  assign controlled_buffer_1_out = in_3 ? {8{1'b0}} : 8'bz;  // Controlled_Buffer controlled_buffer_1
  assign controlled_buffer_2_out = in_14 ? register_1_q : 8'bz;  // Controlled_Buffer controlled_buffer_2
  Register register_1 (.D(out_19), .en(in_10), .Q(register_1_q), .clk(in_13), .clr(in_18));
  Register register_2 (.D(out_19), .en(in_12), .Q(register_2_q), .clk(in_13), .clr(in_18));
  assign controlled_buffer_2_out = in_2 ? in_1 : 8'bz;  // Controlled_Buffer controlled_buffer_3
  assign controlled_buffer_1_out = in_15 ? register_1_q : 8'bz;  // Controlled_Buffer controlled_buffer_4
  assign controlled_buffer_2_out = in_16 ? register_2_q : 8'bz;  // Controlled_Buffer controlled_buffer_5
  assign controlled_buffer_1_out = in_17 ? register_2_q : 8'bz;  // Controlled_Buffer controlled_buffer_6
  alu8 alu8_1 (
    .rsl(in_11), .lsr(in_9), .\xor (in_8), .\or (in_7), .\and (in_6), .addsub(in_5), .sub(in_4),
    .b(controlled_buffer_2_out), .a(controlled_buffer_1_out), .x(out_19));  // open: cout
endmodule

module latch1 (
  input  in_1,
  input  in_2,
  input  in_3,
  output out_4
);

  wire and_1_out, and_2_out, nor_1_out, not_1_out, or_1_out;

  not not_1 (not_1_out, in_1);
  and and_1 (and_1_out, in_1, in_2);
  and and_2 (and_2_out, in_2, not_1_out);
  nor nor_1 (nor_1_out, and_1_out, out_4);
  nor nor_2 (out_4, nor_1_out, or_1_out);
  or or_1 (or_1_out, and_2_out, in_3);
endmodule
