// Logisim project stream3-fixed2.circ as structural Verilog
module fulladd (
  input  in_1,
  input  in_2,
  input  in_3,
  output out_4,
  output out_5
);

  wire and_1_out, and_2_out, and_3_out;

  and and_1 (and_1_out, in_1, in_2);
  and and_2 (and_2_out, in_1, in_3);
  and and_3 (and_3_out, in_2, in_3);
  xor xor_1 (out_5, in_1, in_2, in_3);
  or or_1 (out_4, and_1_out, and_2_out, and_3_out);
endmodule

module alu8 (
  input  rsl,
  input  lsr,
  input  \xor ,
  input  \or ,
  input  \and ,
  input  add,
  input  sub,
  input  [7:0] b,
  input  [7:0] a,
  output [7:0] x,
  output out_11,
  output out_12,
  output out_13
);

  wire or_2_out;
  wire [7:0] adder_1_out, and_1_out, bit_extender_1_out, leftshift8_1_out_2, or_1_out, rightshift8_1_out_2,
       xor_1_out, xor_2_out;

  assign bit_extender_1_out = {{7{sub}}, sub};  // Bit_Extender bit_extender_1
  assign xor_1_out = bit_extender_1_out ^ b;  // XOR_Gate xor_1, 8 bits wide
  Adder adder_1 (.a(xor_1_out), .b(a), .out(adder_1_out), .cin(sub), .cout(out_11));
  assign and_1_out = b & a;  // AND_Gate and_1, 8 bits wide
  assign or_1_out = b | a;  // OR_Gate or_1, 8 bits wide
  assign xor_2_out = b ^ a;  // XOR_Gate xor_2, 8 bits wide
  leftshift8 leftshift8_1 (.in_1(a), .out_2(leftshift8_1_out_2));
  rightshift8 rightshift8_1 (.in_1(a), .out_2(rightshift8_1_out_2));
  or or_2 (or_2_out, add, sub);
  assign {out_13, x[6:0]} = or_2_out ? adder_1_out : 8'bz;  // Controlled_Buffer controlled_buffer_1
  assign {out_13, x[6:0]} = \and  ? and_1_out : 8'bz;  // Controlled_Buffer controlled_buffer_2
  assign {out_13, x[6:0]} = \or  ? or_1_out : 8'bz;  // Controlled_Buffer controlled_buffer_3
  assign {out_13, x[6:0]} = \xor  ? xor_2_out : 8'bz;  // Controlled_Buffer controlled_buffer_4
  assign {out_13, x[6:0]} = lsr ? leftshift8_1_out_2 : 8'bz;  // Controlled_Buffer controlled_buffer_5
  assign {out_13, x[6:0]} = rsl ? rightshift8_1_out_2 : 8'bz;  // Controlled_Buffer controlled_buffer_6
  and and_2 (out_12, x[0], x[1], x[2], x[3], x[5], x[6], out_13, x[4]);

  assign x[7] = out_13;
endmodule

module add4 (
  input  [3:0] in_1,
  input  [3:0] in_2,
  input  in_3,
  output out_4,
  output [3:0] out_5
);

  wire fulladd_2_out_4, fulladd_3_out_4, fulladd_4_out_4;

  fulladd fulladd_1 (.in_1(in_1[3]), .in_2(in_2[3]), .in_3(fulladd_2_out_4), .out_4(out_4), .out_5(out_5[3]));
  fulladd fulladd_2 (.in_1(in_1[2]), .in_2(in_2[2]), .in_3(fulladd_3_out_4), .out_4(fulladd_2_out_4), .out_5(out_5[2]));
  fulladd fulladd_3 (.in_1(in_1[1]), .in_2(in_2[1]), .in_3(fulladd_4_out_4), .out_4(fulladd_3_out_4), .out_5(out_5[1]));
  fulladd fulladd_4 (.in_1(in_1[0]), .in_2(in_2[0]), .in_3(in_3), .out_4(fulladd_4_out_4), .out_5(out_5[0]));
endmodule

module leftshift8 (
  input  [7:0] in_1,
  output [7:0] out_2
);


  assign out_2 = {in_1[6:0], 1'b0};
endmodule

module rightshift8 (
  input  [7:0] in_1,
  output [7:0] out_2
);


  assign out_2 = {1'b0, in_1[7:1]};
endmodule

module top (
  input  in_1,
  input  in_2
);

  wire alu8_1_out_11, alu8_1_out_12, alu8_1_out_13, decoder_1_out0, decoder_1_out1, decoder_1_out2,
       decoder_1_out3, decoder_1_out4, decoder_1_out5, decoder_1_out6;
  wire [1:0] undriven_2;
  wire [2:0] d_ff_1_q;
  wire [2:1] undriven_5, undriven_6;
  wire [2:2] undriven_3, undriven_4;
  wire [7:0] alu8_1_x, controlled_buffer_1_out, counter_1_q, multiplexer_1_out, multiplexer_2_out,
       multiplexer_3_out, register_1_q, register_2_q;
  wire [19:0] undriven;

  Register register_1 (.D(alu8_1_x), .en(undriven_2[0]), .Q(register_1_q), .clk(in_2), .clr(in_1));
  Register register_2 (.D(alu8_1_x), .en(undriven[8]), .Q(register_2_q), .clk(in_2), .clr(in_1));
  Multiplexer #(.select(3), .width(8), .enable("false")) multiplexer_1 (
    .in0(register_1_q), .in1(register_2_q), .in2(controlled_buffer_1_out), .out(multiplexer_1_out),
    .sel({undriven_6, undriven[3]}));  // open: in3, in4, in5, in6, in7
  Multiplexer #(.select(3), .width(8), .enable("false")) multiplexer_2 (
    .in0(register_1_q), .in1(register_2_q), .in2({8{1'b0}}), .out(multiplexer_2_out), .sel(undriven[2:0]));  // open: in3, in4, in5, in6, in7
  Decoder #(.select(3), .enable("false")) decoder_1 (
    .out0(decoder_1_out0), .out1(decoder_1_out1), .out2(decoder_1_out2), .out3(decoder_1_out3),
    .out4(decoder_1_out4), .out5(decoder_1_out5), .out6(decoder_1_out6), .sel({undriven_3[2], undriven[5:4]}));  // open: out7
  alu8 alu8_1 (
    .rsl(decoder_1_out6), .lsr(decoder_1_out5), .\xor (decoder_1_out4), .\or (decoder_1_out3),
    .\and (decoder_1_out2), .add(decoder_1_out1), .sub(decoder_1_out0), .b(multiplexer_2_out),
    .a(multiplexer_1_out), .x(alu8_1_x), .out_11(alu8_1_out_11), .out_12(alu8_1_out_12),
    .out_13(alu8_1_out_13));
  Counter counter_1 (
    .load(undriven[14]), .D(alu8_1_x), .count(undriven[16]), .Q(counter_1_q), .clk(in_2), .clr(in_1));  // open: carry
  D_Flip_Flop d_ff_1 (
    .clk(in_2), .D(alu8_1_out_12), .Q(d_ff_1_q[0]), .en(undriven_4[2]), .reset(in_1));  // open: Qn, preset
  D_Flip_Flop d_ff_2 (
    .clk(in_2), .D(alu8_1_out_11), .Q(d_ff_1_q[1]), .en(undriven[11]), .reset(in_1));  // open: Qn, preset
  assign controlled_buffer_1_out = undriven[12] ? alu8_1_x : 8'bz;  // Controlled_Buffer controlled_buffer_1
  Multiplexer #(.select(3), .width(8), .enable("false")) multiplexer_3 (
    .in0(multiplexer_1_out), .in1(multiplexer_2_out), .in2(counter_1_q), .out(multiplexer_3_out),
    .sel({undriven_5, undriven[19]}));  // open: in3, in4, in5, in6, in7
  D_Flip_Flop d_ff_3 (
    .clk(in_2), .D(alu8_1_out_13), .Q(d_ff_1_q[2]), .en(undriven[10]), .reset(in_1));  // open: Qn, preset
  RAM ram_1 (
    .addr(multiplexer_3_out), .data(controlled_buffer_1_out), .sel(1'b1), .clk(in_2), .ld(undriven[18]));  // open: clr
  // Pins of 1 and 2 bits meet at undriven_2
  // Pins of 1 and 3 bits meet at {undriven_6, undriven[3]}
  // Pins of 2 and 3 bits meet at {undriven_4[2], undriven[11:10]}
  // Pins of 1 and 2 bits meet at undriven[9:8]
  // Pins of 1 and 2 bits meet at undriven[15:14]
  // Pins of 1 and 2 bits meet at undriven[17:16]
  // Pins of 2 and 3 bits meet at {undriven_3[2], undriven[5:4]}
  // Pins of 1 and 2 bits meet at undriven[13:12]
  // Pins of 1 and 3 bits meet at {undriven_5, undriven[19]}
endmodule

module latch1 (
  input  in_1,
  input  in_2,
  input  in_3,
  output out_4
);

  wire and_1_out, and_2_out, nor_1_out, not_1_out, or_1_out;

  not not_1 (not_1_out, in_1);
  and and_1 (and_1_out, in_1, in_2);
  and and_2 (and_2_out, in_2, not_1_out);
  nor nor_1 (nor_1_out, and_1_out, out_4);
  nor nor_2 (out_4, nor_1_out, or_1_out);
  or or_1 (or_1_out, and_2_out, in_3);
endmodule

module counter (
  input  d,
  input  t,
  input  l,
  input  clk,
  output out_5,
  output out_6
);

  wire and_1_out, multiplexer_1_out, or_1_out;

  Multiplexer #(.enable("false")) multiplexer_1 (.in0(d), .in1(out_6), .out(multiplexer_1_out), .sel(and_1_out));
  and and_1 (and_1_out, t, ~l);  // AND_Gate
  or or_1 (or_1_out, t, l);
  D_Flip_Flop d_ff_1 (.clk(clk), .D(multiplexer_1_out), .Q(out_5), .Qn(out_6), .en(or_1_out));  // open: preset, reset
endmodule

module counter2 (
  input  in_1,
  input  in_2,
  input  in_3,
  input  in_4,
  input  in_5,
  input  in_6,
  input  in_7
);

  wire and_1_out, and_2_out, and_3_out, counter_1_out_5, counter_2_out_5, counter_3_out_5, counter_4_out_5;

  counter counter_1 (.l(in_3), .t(in_1), .clk(in_2), .out_5(counter_1_out_5), .d(in_4));  // open: out_6
  and and_1 (and_1_out, in_1, counter_1_out_5);
  and and_2 (and_2_out, and_1_out, counter_2_out_5);
  counter counter_2 (.l(in_3), .t(and_1_out), .clk(in_2), .out_5(counter_2_out_5), .d(in_5));  // open: out_6
  counter counter_3 (.l(in_3), .t(and_2_out), .clk(in_2), .out_5(counter_3_out_5), .d(in_6));  // open: out_6
  and and_3 (and_3_out, and_2_out, counter_3_out_5);
  counter counter_4 (.l(in_3), .t(and_3_out), .clk(in_2), .out_5(counter_4_out_5), .d(in_7));  // open: out_6
endmodule
