// Logisim project stream3prime.circ as structural Verilog: 4 circuits, main circuit computer
module alu8 (
  input  rsl,
  input  lsr,
  input  \xor ,
  input  \or ,
  input  \and ,
  input  add,
  input  sub,
  input  [7:0] b,
  input  [7:0] a,
  output [7:0] x,
  output out_11,
  output out_12,
  output out_13
);

  wire or_2_out;
  wire [7:0] adder_1_out, and_1_out, bit_extender_1_out, leftshift8_1_out_2, or_1_out, rightshift8_1_out_2,
       xor_1_out, xor_2_out;

  assign bit_extender_1_out = {{7{sub}}, sub};  // Bit_Extender bit_extender_1
  assign xor_1_out = bit_extender_1_out ^ b;  // XOR_Gate xor_1, 8 bits wide
  Adder adder_1 (.a(xor_1_out), .b(a), .out(adder_1_out), .cin(sub), .cout(out_11));
  assign and_1_out = b & a;  // AND_Gate and_1, 8 bits wide
  assign or_1_out = b | a;  // OR_Gate or_1, 8 bits wide
  assign xor_2_out = b ^ a;  // XOR_Gate xor_2, 8 bits wide
  leftshift8 leftshift8_1 (.in_1(a), .out_2(leftshift8_1_out_2));
  rightshift8 rightshift8_1 (.in_1(a), .out_2(rightshift8_1_out_2));
  or or_2 (or_2_out, add, sub);
  assign {out_13, x[6:0]} = or_2_out ? adder_1_out : 8'bz;  // Controlled_Buffer controlled_buffer_1
  assign {out_13, x[6:0]} = \and  ? and_1_out : 8'bz;  // Controlled_Buffer controlled_buffer_2
  assign {out_13, x[6:0]} = \or  ? or_1_out : 8'bz;  // Controlled_Buffer controlled_buffer_3
  assign {out_13, x[6:0]} = \xor  ? xor_2_out : 8'bz;  // Controlled_Buffer controlled_buffer_4
  assign {out_13, x[6:0]} = lsr ? leftshift8_1_out_2 : 8'bz;  // Controlled_Buffer controlled_buffer_5
  assign {out_13, x[6:0]} = rsl ? rightshift8_1_out_2 : 8'bz;  // Controlled_Buffer controlled_buffer_6
  and and_2 (out_12, x[0], x[1], x[2], x[3], x[5], x[6], out_13, x[4]);

  assign x[7] = out_13;
endmodule

module leftshift8 (
  input  [7:0] in_1,
  output [7:0] out_2
);


  assign out_2 = {in_1[6:0], 1'b0};
endmodule

module rightshift8 (
  input  [7:0] in_1,
  output [7:0] out_2
);


  assign out_2 = {1'b0, in_1[7:1]};
endmodule

module computer (
  input  clr,
  input  clk
);

  wire alu8_1_out_11, alu8_1_out_12, alu8_1_out_13, decoder_1_out0, decoder_1_out1, decoder_1_out2,
       decoder_1_out3, decoder_1_out4, decoder_1_out5, decoder_1_out6;
  wire [2:0] d_ff_1_q, undriven_2;
  wire [7:0] alu8_1_x, controlled_buffer_1_out, counter_1_q, multiplexer_1_out, multiplexer_2_out,
       multiplexer_3_out, register_1_q, register_2_q;
  wire [20:0] undriven;

  Register register_1 (.D(alu8_1_x), .en(undriven[0]), .Q(register_1_q), .clk(clk), .clr(clr));
  Register register_2 (.D(alu8_1_x), .en(undriven[1]), .Q(register_2_q), .clk(clk), .clr(clr));
  Multiplexer #(.select(3), .width(8), .enable("false")) multiplexer_1 (
    .in0(register_1_q), .in1(register_2_q), .in2(controlled_buffer_1_out), .out(multiplexer_1_out),
    .sel(undriven[7:5]));  // open: in3, in4, in5, in6, in7
  Multiplexer #(.select(3), .width(8), .enable("false")) multiplexer_2 (
    .in0(register_1_q), .in1(register_2_q), .in2({8{1'b0}}), .out(multiplexer_2_out), .sel(undriven[4:2]));  // open: in3, in4, in5, in6, in7
  Decoder #(.select(3), .enable("false")) decoder_1 (
    .out0(decoder_1_out0), .out1(decoder_1_out1), .out2(decoder_1_out2), .out3(decoder_1_out3),
    .out4(decoder_1_out4), .out5(decoder_1_out5), .out6(decoder_1_out6), .sel(undriven[10:8]));  // open: out7
  Counter counter_1 (
    .load(undriven[15]), .D(alu8_1_x), .count(undriven[16]), .Q(counter_1_q), .clk(clk), .clr(clr));  // open: carry
  alu8 alu8_1 (
    .rsl(decoder_1_out6), .lsr(decoder_1_out5), .\xor (decoder_1_out4), .\or (decoder_1_out3),
    .\and (decoder_1_out2), .add(decoder_1_out1), .sub(decoder_1_out0), .b(multiplexer_2_out),
    .a(multiplexer_1_out), .x(alu8_1_x), .out_11(alu8_1_out_11), .out_12(alu8_1_out_12),
    .out_13(alu8_1_out_13));
  D_Flip_Flop d_ff_1 (
    .clk(clk), .D(alu8_1_out_12), .Q(d_ff_1_q[0]), .en(undriven_2[2]), .reset(clr));  // open: Qn, preset
  Multiplexer #(.select(3), .width(8), .enable("false")) multiplexer_3 (
    .in0(multiplexer_1_out), .in1(multiplexer_2_out), .in2(counter_1_q), .out(multiplexer_3_out),
    .sel(undriven[19:17]));  // open: in3, in4, in5, in6, in7
  D_Flip_Flop d_ff_2 (
    .clk(clk), .D(alu8_1_out_11), .Q(d_ff_1_q[1]), .en(undriven_2[1]), .reset(clr));  // open: Qn, preset
  assign controlled_buffer_1_out = undriven[14] ? alu8_1_x : 8'bz;  // Controlled_Buffer controlled_buffer_1
  D_Flip_Flop d_ff_3 (
    .clk(clk), .D(alu8_1_out_13), .Q(d_ff_1_q[2]), .en(undriven_2[0]), .reset(clr));  // open: Qn, preset
  RAM ram_1 (
    .addr(multiplexer_3_out), .data(controlled_buffer_1_out), .sel(1'b1), .clk(clk), .ld(undriven[20]));  // open: clr

  // Notes on the sheet:
  //   counter register fixed
  //   carry out of shift
  //   fix the zero flag
  //   a
  //   b
  //   F-bus
  //   ip
  //   z
  //   c
  //   A-Bus
  //   s
  //   D-bus
endmodule
