// Logisim project stream5.circ as structural Verilog: 4 circuits, main circuit computer
module alu8 (
  input  rsl,
  input  lsr,
  input  \xor ,
  input  \or ,
  input  \and ,
  input  add,
  input  sub,
  input  [7:0] b,
  input  [7:0] a,
  output [7:0] x,
  output out_11,
  output out_12,
  output out_13
);

  wire adder_1_cout, leftshift8_1_out_3, or_2_out, rightshift8_1_out_2;
  wire [7:0] adder_1_out, and_1_out, bit_extender_1_out, leftshift8_1_out_2, or_1_out, rightshift8_1_out_3,
       xor_1_out, xor_2_out;

  assign bit_extender_1_out = {{7{sub}}, sub};  // Bit_Extender bit_extender_1
  assign xor_1_out = bit_extender_1_out ^ b;  // XOR_Gate xor_1, 8 bits wide
  Adder adder_1 (.a(xor_1_out), .b(a), .out(adder_1_out), .cin(sub), .cout(adder_1_cout));
  assign and_1_out = b & a;  // AND_Gate and_1, 8 bits wide
  assign or_1_out = b | a;  // OR_Gate or_1, 8 bits wide
  assign xor_2_out = b ^ a;  // XOR_Gate xor_2, 8 bits wide
  leftshift8 leftshift8_1 (.in_1(a), .out_2(leftshift8_1_out_2), .out_3(leftshift8_1_out_3));
  rightshift8 rightshift8_1 (.in_1(a), .out_3(rightshift8_1_out_3), .out_2(rightshift8_1_out_2));
  or or_2 (or_2_out, add, sub);
  assign out_11 = or_2_out ? adder_1_cout : 1'bz;  // Controlled_Buffer controlled_buffer_1
  assign out_11 = rsl ? rightshift8_1_out_2 : 1'bz;  // Controlled_Buffer controlled_buffer_2
  assign out_11 = lsr ? leftshift8_1_out_3 : 1'bz;  // Controlled_Buffer controlled_buffer_3
  assign {out_13, x[6:0]} = or_2_out ? adder_1_out : 8'bz;  // Controlled_Buffer controlled_buffer_4
  assign {out_13, x[6:0]} = \and  ? and_1_out : 8'bz;  // Controlled_Buffer controlled_buffer_5
  assign {out_13, x[6:0]} = \or  ? or_1_out : 8'bz;  // Controlled_Buffer controlled_buffer_6
  assign {out_13, x[6:0]} = \xor  ? xor_2_out : 8'bz;  // Controlled_Buffer controlled_buffer_7
  assign {out_13, x[6:0]} = lsr ? leftshift8_1_out_2 : 8'bz;  // Controlled_Buffer controlled_buffer_8
  assign {out_13, x[6:0]} = rsl ? rightshift8_1_out_3 : 8'bz;  // Controlled_Buffer controlled_buffer_9
  nor nor_1 (out_12, x[0], x[1], x[2], x[3], x[5], x[6], out_13, x[4]);

  assign x[7] = out_13;
endmodule

module leftshift8 (
  input  [7:0] in_1,
  output [7:0] out_2,
  output out_3
);


  assign out_2 = {in_1[6:0], 1'b0};
  assign out_3 = in_1[7];
endmodule

module rightshift8 (
  input  [7:0] in_1,
  output out_2,
  output [7:0] out_3
);


  assign out_2 = in_1[0];
  assign out_3 = {1'b0, in_1[7:1]};
endmodule

module computer (
  input  clr,
  input  clk
);

  wire alu8_1_out_11, alu8_1_out_12, alu8_1_out_13, and_1_out, and_2_out, and_3_out, and_4_out, and_5_out,
       and_6_out, and_7_out, and_8_out, and_9_out, and_10_out, and_11_out, and_12_out,
       controlled_buffer_3_out, d_ff_3_q, decoder_1_out0, decoder_1_out1, decoder_1_out2, decoder_1_out3,
       decoder_1_out4, decoder_1_out5, decoder_1_out6, xnor_1_out;
  wire [0:0] d_ff_1_q, multiplexer_4_out_2, not_2_out, not_3_out;
  wire [2:0] controlled_buffer_1_out_2, controlled_buffer_1_out_3, controlled_buffer_1_out_4,
       controlled_buffer_1_out_5, controlled_buffer_1_out_6, d_ff_2_q, undriven_2, undriven_3;
  wire [7:0] alu8_1_x, controlled_buffer_10_out, counter_1_q, multiplexer_1_out, multiplexer_2_out,
       multiplexer_3_out, register_1_q, register_2_q, register_3_q;
  wire [7:2] multiplexer_4_out_3;
  wire [13:0] undriven;
  wire [17:17] multiplexer_4_out;
  wire [20:0] controlled_buffer_1_out, not_1_out;
  wire [20:11] undriven_4, undriven_5, undriven_6;

  Register register_1 (.D(alu8_1_x), .en(controlled_buffer_1_out[0]), .Q(register_1_q), .clk(clk), .clr(clr));
  Register register_2 (.D(alu8_1_x), .en(controlled_buffer_1_out[1]), .Q(register_2_q), .clk(clk), .clr(clr));
  // Probe on {controlled_buffer_1_out[20], controlled_buffer_1_out_6, controlled_buffer_1_out[16:14], controlled_buffer_1_out_5, controlled_buffer_1_out_4, controlled_buffer_1_out_3, controlled_buffer_1_out_2, controlled_buffer_1_out[1:0]}
  Multiplexer #(.select(3), .width(8), .enable("false")) multiplexer_1 (
    .in0(register_1_q), .in1(register_2_q), .in2(controlled_buffer_10_out), .out(multiplexer_1_out),
    .sel(controlled_buffer_1_out_3));  // open: in3, in4, in5, in6, in7
  Multiplexer #(.select(3), .width(8), .enable("false")) multiplexer_2 (
    .in0(register_1_q), .in1(register_2_q), .in2({8{1'b0}}), .out(multiplexer_2_out),
    .sel(controlled_buffer_1_out_2));  // open: in3, in4, in5, in6, in7
  assign {controlled_buffer_1_out[20], controlled_buffer_1_out_6, controlled_buffer_1_out[16:14], controlled_buffer_1_out_5, controlled_buffer_1_out_4, controlled_buffer_1_out_3, controlled_buffer_1_out_2, controlled_buffer_1_out[1:0]} = d_ff_1_q[0] ? {7'b1010100, undriven} : 21'bz;  // Controlled_Buffer controlled_buffer_1
  D_Flip_Flop d_ff_1 (.clk(clk), .D(controlled_buffer_3_out), .Q(d_ff_1_q[0]), .preset(clr));  // open: Qn, en, reset
  and and_1 (and_1_out, and_2_out, ~xnor_1_out);  // AND_Gate
  assign {controlled_buffer_1_out[20], controlled_buffer_1_out_6, controlled_buffer_1_out[16:14], controlled_buffer_1_out_5, controlled_buffer_1_out_4, controlled_buffer_1_out_3, controlled_buffer_1_out_2, controlled_buffer_1_out[1:0]} = and_1_out ? {not_1_out[20], undriven_3, not_1_out[16:14], undriven_2, 5'b00100, multiplexer_4_out_2[0], 3'b010, multiplexer_4_out[17], not_1_out[0]} : 21'bz;  // Controlled_Buffer controlled_buffer_2
  and and_2 (and_2_out, and_10_out, d_ff_1_q[0]);
  assign controlled_buffer_3_out = and_1_out ? 1'b1 : 1'bz;  // Controlled_Buffer controlled_buffer_3
  and and_3 (and_3_out, and_11_out, d_ff_1_q[0]);
  assign {controlled_buffer_1_out[20], controlled_buffer_1_out_6, controlled_buffer_1_out[16:14], controlled_buffer_1_out_5, controlled_buffer_1_out_4, controlled_buffer_1_out_3, controlled_buffer_1_out_2, controlled_buffer_1_out[1:0]} = and_3_out ? {undriven_4, {11{1'b0}}} : 21'bz;  // Controlled_Buffer controlled_buffer_4
  and and_4 (and_4_out, and_12_out, d_ff_1_q[0]);
  assign {controlled_buffer_1_out[20], controlled_buffer_1_out_6, controlled_buffer_1_out[16:14], controlled_buffer_1_out_5, controlled_buffer_1_out_4, controlled_buffer_1_out_3, controlled_buffer_1_out_2, controlled_buffer_1_out[1:0]} = and_4_out ? {undriven_5, {11{1'b0}}} : 21'bz;  // Controlled_Buffer controlled_buffer_5
  not not_1 (not_1_out[0], multiplexer_4_out[17]);
  assign controlled_buffer_3_out = and_3_out ? 1'b0 : 1'bz;  // Controlled_Buffer controlled_buffer_6
  assign controlled_buffer_3_out = and_4_out ? 1'b0 : 1'bz;  // Controlled_Buffer controlled_buffer_7
  Decoder #(.select(3), .enable("false")) decoder_1 (
    .out0(decoder_1_out0), .out1(decoder_1_out1), .out2(decoder_1_out2), .out3(decoder_1_out3),
    .out4(decoder_1_out4), .out5(decoder_1_out5), .out6(decoder_1_out6), .sel(controlled_buffer_1_out_4));  // open: out7
  and and_5 (and_5_out, d_ff_1_q[0], ~controlled_buffer_3_out);  // AND_Gate
  xnor xnor_1 (xnor_1_out, multiplexer_4_out[17], multiplexer_4_out_2[0]);
  and and_6 (and_6_out, and_2_out, xnor_1_out);
  Counter counter_1 (
    .load(controlled_buffer_1_out[15]), .D(alu8_1_x), .count(controlled_buffer_1_out[16]), .Q(counter_1_q),
    .clk(clk), .clr(clr));  // open: carry
  assign {controlled_buffer_1_out[20], controlled_buffer_1_out_6, controlled_buffer_1_out[16:14], controlled_buffer_1_out_5, controlled_buffer_1_out_4, controlled_buffer_1_out_3, controlled_buffer_1_out_2, controlled_buffer_1_out[1:0]} = and_6_out ? {undriven_6, {11{1'b0}}} : 21'bz;  // Controlled_Buffer controlled_buffer_8
  alu8 alu8_1 (
    .rsl(decoder_1_out6), .lsr(decoder_1_out5), .\xor (decoder_1_out4), .\or (decoder_1_out3),
    .\and (decoder_1_out2), .add(decoder_1_out1), .sub(decoder_1_out0), .b(multiplexer_2_out),
    .a(multiplexer_1_out), .x(alu8_1_x), .out_11(alu8_1_out_11), .out_12(alu8_1_out_12),
    .out_13(alu8_1_out_13));
  // Probe on controlled_buffer_1_out_6
  assign controlled_buffer_3_out = and_6_out ? 1'b0 : 1'bz;  // Controlled_Buffer controlled_buffer_9
  D_Flip_Flop d_ff_2 (
    .clk(clk), .D(alu8_1_out_12), .Q(d_ff_2_q[0]), .en(controlled_buffer_1_out_5[2]), .reset(clr));  // open: Qn, preset
  Multiplexer #(.select(3), .width(8), .enable("false")) multiplexer_3 (
    .in0(register_1_q), .in1(register_2_q), .in2(counter_1_q), .out(multiplexer_3_out),
    .sel(controlled_buffer_1_out_6));  // open: in3, in4, in5, in6, in7
  D_Flip_Flop d_ff_3 (.clk(clk), .D(and_5_out), .Q(d_ff_3_q), .reset(clr));  // open: Qn, preset, en
  and and_7 (and_7_out, and_10_out, d_ff_3_q);
  and and_8 (and_8_out, and_11_out, d_ff_3_q);
  and and_9 (and_9_out, and_12_out, d_ff_3_q);
  D_Flip_Flop d_ff_4 (
    .clk(clk), .D(alu8_1_out_11), .Q(d_ff_2_q[1]), .en(controlled_buffer_1_out_5[1]), .reset(clr));  // open: Qn, preset
  assign controlled_buffer_10_out = controlled_buffer_1_out[14] ? alu8_1_x : 8'bz;  // Controlled_Buffer controlled_buffer_10
  assign {controlled_buffer_1_out[20], controlled_buffer_1_out_6, controlled_buffer_1_out[16:14], controlled_buffer_1_out_5, controlled_buffer_1_out_4, controlled_buffer_1_out_3, controlled_buffer_1_out_2, controlled_buffer_1_out[1:0]} = and_7_out ? {19'h54052, multiplexer_4_out[17], not_3_out[0]} : 21'bz;  // Controlled_Buffer controlled_buffer_11
  assign {controlled_buffer_1_out[20], controlled_buffer_1_out_6, controlled_buffer_1_out[16:14], controlled_buffer_1_out_5, controlled_buffer_1_out_4, controlled_buffer_1_out_3, controlled_buffer_1_out_2, controlled_buffer_1_out[1:0]} = and_8_out ? {3'b000, multiplexer_4_out[17], 11'h104, multiplexer_4_out_2[0], 5'b01000} : 21'bz;  // Controlled_Buffer controlled_buffer_12
  not not_2 (not_2_out[0], multiplexer_4_out[17]);
  assign {controlled_buffer_1_out[20], controlled_buffer_1_out_6, controlled_buffer_1_out[16:14], controlled_buffer_1_out_5, controlled_buffer_1_out_4, controlled_buffer_1_out_3, controlled_buffer_1_out_2, controlled_buffer_1_out[1:0]} = and_9_out ? {3'b100, multiplexer_4_out_2[0], 15'h52, multiplexer_4_out[17], not_2_out[0]} : 21'bz;  // Controlled_Buffer controlled_buffer_13
  D_Flip_Flop d_ff_5 (
    .clk(clk), .D(alu8_1_out_13), .Q(d_ff_2_q[2]), .en(controlled_buffer_1_out_5[0]), .reset(clr));  // open: Qn, preset
  not not_3 (not_3_out[0], multiplexer_4_out[17]);
  assign controlled_buffer_3_out = and_7_out ? 1'b1 : 1'bz;  // Controlled_Buffer controlled_buffer_14
  assign controlled_buffer_3_out = and_8_out ? 1'b1 : 1'bz;  // Controlled_Buffer controlled_buffer_15
  assign controlled_buffer_3_out = and_9_out ? 1'b1 : 1'bz;  // Controlled_Buffer controlled_buffer_16
  RAM ram_1 (
    .addr(multiplexer_3_out), .data(controlled_buffer_10_out), .sel(1'b1), .clk(clk),
    .ld(controlled_buffer_1_out[20]));  // open: clr
  Register register_3 (.D(controlled_buffer_10_out), .Q(register_3_q), .clk(clk));  // open: en, clr
  // Probe on controlled_buffer_10_out
  Multiplexer #(.select(2), .width(8), .enable("false")) multiplexer_4 (
    .in0(register_3_q), .in1(controlled_buffer_10_out), .in2({8{1'b1}}), .in3({8{1'b1}}),
    .out({multiplexer_4_out_3, multiplexer_4_out[17], multiplexer_4_out_2[0]}), .sel({clr, d_ff_1_q[0]}));
  and and_10 (and_10_out, ~multiplexer_4_out_3[2], ~multiplexer_4_out_3[3], ~multiplexer_4_out_3[4], ~multiplexer_4_out_3[5], ~multiplexer_4_out_3[6], ~multiplexer_4_out_3[7]);  // AND_Gate
  and and_11 (and_11_out, ~multiplexer_4_out_3[2], multiplexer_4_out_3[3], ~multiplexer_4_out_3[4], ~multiplexer_4_out_3[5], ~multiplexer_4_out_3[6], ~multiplexer_4_out_3[7]);  // AND_Gate
  and and_12 (and_12_out, multiplexer_4_out_3[2], ~multiplexer_4_out_3[3], ~multiplexer_4_out_3[4], ~multiplexer_4_out_3[5], ~multiplexer_4_out_3[6], ~multiplexer_4_out_3[7]);  // AND_Gate

  // Notes on the sheet:
  //   a
  //   b
  //   F-bus
  //   mov r,r / mov r,imm
  //   mov [r],r
  //   mov r,[r]
  //   ip
  //   z
  //   c
  //   A-Bus
  //   s
  //   D-bus
endmodule
